// Logisim project Guia0501.circ as structural Verilog: 1 circuit, main circuit main
module main (
  input  a,
  input  b,
  input  a_2,
  input  b_2,
  output out_5,
  output out_6
);

  wire nor_1_out, nor_2_out, nor_3_out, nor_4_out, not_1_out;

  not not_1 (not_1_out, b);
  and and_1 (out_5, a, not_1_out);
  nor nor_1 (nor_1_out, a_2, a_2);
  nor nor_2 (nor_2_out, a_2, a_2);
  nor nor_3 (nor_3_out, a_2, nor_1_out);
  nor nor_4 (nor_4_out, a_2, nor_2_out);
  nor nor_5 (out_6, nor_3_out, nor_4_out);

  assign b_2 = a_2;
endmodule
