// Logisim project Guia0502.circ as structural Verilog: 1 circuit, main circuit main
module main (
  input  in_1,
  input  in_2,
  input  a,
  input  b,
  output out_5,
  output out_6
);

  wire not_1_out, not_2_out;

  not not_1 (not_1_out, in_1);
  not not_2 (not_2_out, b);
  or or_1 (out_5, not_1_out, in_2);
  nand nand_1 (out_6, a, not_2_out);

  // Notes on the sheet:
  //   S = ~a | b
  //   S = (a) NAND (~b)
endmodule
