// Logisim project Guia0504.circ as structural Verilog: 1 circuit, main circuit main
module main (
  input  in_1,
  input  in_2,
  output out_3
);

  wire and_1_out, not_1_out;

  not not_1 (not_1_out, in_2);
  not not_2 (out_3, and_1_out);
  and and_1 (and_1_out, in_1, not_1_out);

  // Notes on the sheet:
  //   S = ~(a & ~b)
endmodule
