// Logisim project Guia_0701.circ as structural Verilog: 1 circuit, main circuit main
module main (
  input  A,
  input  B,
  input  in_3,
  output S
);

  wire and_1_out, and_2_out, and_3_out, nand_1_out, not_1_out;

  and and_1 (and_1_out, A, B);
  nand nand_1 (nand_1_out, A, B);
  not not_1 (not_1_out, in_3);
  and and_2 (and_2_out, and_1_out, not_1_out);
  and and_3 (and_3_out, nand_1_out, in_3);
  or or_1 (S, and_2_out, and_3_out);

  // Notes on the sheet:
  //   Felipe Gabriel de Carvalho - 1543536
endmodule
