// Logisim project Guia_0703.circ as structural Verilog: 1 circuit, main circuit main
module main (
  input  in_1,
  input  in_2,
  input  in_3,
  input  in_4,
  output out_5
);

  wire and_1_out, and_2_out, and_3_out, and_4_out, and_5_out, and_6_out, and_7_out, nand_1_out, nor_1_out,
       not_1_out, not_2_out, or_1_out;

  and and_1 (and_1_out, in_1, in_2);
  nand nand_1 (nand_1_out, in_1, in_2);
  not not_1 (not_1_out, in_3);
  or or_1 (or_1_out, in_1, in_2);
  and and_2 (and_2_out, and_1_out, not_1_out);
  and and_3 (and_3_out, nand_1_out, in_3);
  nor nor_1 (nor_1_out, in_1, in_2);
  // OR_Gate or_2 has open pins: in0=and_2_out, in1=and_3_out, out=open
  and and_4 (and_4_out, nor_1_out, in_3);
  and and_5 (and_5_out, or_1_out, not_1_out);
  and and_6 (and_6_out, and_5_out, in_4);
  not not_2 (not_2_out, in_4);
  and and_7 (and_7_out, and_4_out, not_2_out);
  or or_3 (out_5, and_6_out, and_7_out);

  // Notes on the sheet:
  //   Felipe Gabriel de Carvalho - 1543536
endmodule
