// Logisim project Guia_0704.circ as structural Verilog: 1 circuit, main circuit main
module main (
  input  in_1,
  input  in_2,
  input  in_3,
  input  in_4,
  output out_5
);

  wire and_1_out, and_2_out, and_3_out, and_4_out, and_5_out, and_7_out, nor_1_out, not_1_out, not_2_out,
       or_1_out, xnor_1_out, xor_1_out;

  nor nor_1 (nor_1_out, in_1, in_2);
  or or_1 (or_1_out, in_1, in_2);
  xor xor_1 (xor_1_out, in_1, in_2);
  xnor xnor_1 (xnor_1_out, in_1, in_2);
  not not_1 (not_1_out, in_3);
  not not_2 (not_2_out, in_4);
  and and_1 (and_1_out, not_1_out, not_2_out);
  and and_2 (and_2_out, in_3, not_2_out);
  and and_3 (and_3_out, in_4, not_1_out);
  and and_4 (and_4_out, in_3, in_4);
  and and_5 (and_5_out, xnor_1_out, and_1_out);
  and and_6 (and_5_out, xor_1_out, and_2_out);
  and and_7 (and_7_out, or_1_out, and_3_out);
  and and_8 (and_7_out, nor_1_out, and_4_out);
  or or_2 (out_5, and_7_out, and_7_out, and_5_out, and_5_out);

  // Notes on the sheet:
  //   Felipe Gabriel de Carvalho - 1543536
endmodule
