// Logisim project Guia_0801.circ as structural Verilog: 3 circuits, main circuit main
module main (
  input  in_1,
  input  in_2,
  input  in_3,
  input  in_4,
  input  in_5,
  input  in_6,
  input  in_7,
  input  in_8,
  input  in_9,
  input  in_10,
  output out_11,
  output out_12,
  output out_13,
  output out_14,
  output out_15,
  output out_16
);

  wire full_adder_1_carryout, full_adder_2_carryout, full_adder_3_carryout, full_adder_4_carryout;

  Full_Adder full_adder_1 (.CarryIN(1'b0), .in_2(in_1), .in_3(in_2), .Sum(out_11), .CarryOut(full_adder_1_carryout));
  Full_Adder full_adder_2 (
    .CarryIN(full_adder_1_carryout), .in_2(in_3), .in_3(in_4), .Sum(out_12), .CarryOut(full_adder_2_carryout));
  Full_Adder full_adder_3 (
    .CarryIN(full_adder_2_carryout), .in_2(in_5), .in_3(in_6), .Sum(out_13), .CarryOut(full_adder_3_carryout));
  Full_Adder full_adder_4 (
    .CarryIN(full_adder_3_carryout), .in_2(in_7), .in_3(in_8), .Sum(out_14), .CarryOut(full_adder_4_carryout));
  Full_Adder full_adder_5 (.CarryIN(full_adder_4_carryout), .in_2(in_9), .in_3(in_10), .Sum(out_15), .CarryOut(out_16));

  // Notes on the sheet:
  //   Felipe Gabriel de Carvalho - 1543536
endmodule

// HA
module Half_Adder (
  input  in_1,
  input  in_2,
  output sum,
  output carry
);

  xor XOR (sum, in_1, in_2);
  and AND (carry, in_1, in_2);
endmodule

// FA
module Full_Adder (
  input  CarryIN,
  input  in_2,
  input  in_3,
  output Sum,
  output CarryOut
);

  wire half_adder_1_carry, half_adder_1_sum, half_adder_2_carry;

  Half_Adder half_adder_1 (.in_1(in_2), .in_2(in_3), .sum(half_adder_1_sum), .carry(half_adder_1_carry));
  Half_Adder half_adder_2 (.in_1(CarryIN), .in_2(half_adder_1_sum), .sum(Sum), .carry(half_adder_2_carry));
  or or_1 (CarryOut, half_adder_2_carry, half_adder_1_carry);
endmodule
