// Logisim project Guia_0802.circ as structural Verilog: 3 circuits, main circuit main
module main (
  input  in_1,
  input  in_2,
  input  in_3,
  input  in_4,
  input  in_5,
  input  in_6,
  input  in_7,
  input  in_8,
  input  in_9,
  input  in_10,
  input  in_11,
  input  in_12,
  output out_13,
  output out_14,
  output out_15,
  output out_16,
  output out_17,
  output out_18,
  output out_19
);

  wire full_difference_1_carryout, full_difference_2_carryout, full_difference_3_carryout,
       full_difference_4_carryout;

  Full_Difference full_difference_1 (
    .in_1(1'b0), .in_2(in_1), .in_3(in_2), .Diff(out_13), .CarryOut(full_difference_1_carryout));
  Full_Difference full_difference_2 (
    .in_1(full_difference_1_carryout), .in_2(in_3), .in_3(in_4), .Diff(out_14),
    .CarryOut(full_difference_2_carryout));
  Full_Difference full_difference_3 (
    .in_1(full_difference_2_carryout), .in_2(in_5), .in_3(in_6), .Diff(out_15),
    .CarryOut(full_difference_3_carryout));
  Full_Difference full_difference_4 (
    .in_1(full_difference_3_carryout), .in_2(in_7), .in_3(in_8), .Diff(out_16),
    .CarryOut(full_difference_4_carryout));
  Full_Difference full_difference_5 (
    .in_1(full_difference_4_carryout), .in_2(in_9), .in_3(in_10), .Diff(out_17), .CarryOut(out_17));
  Full_Difference full_difference_6 (.in_1(out_17), .in_2(in_11), .in_3(in_12), .Diff(out_18), .CarryOut(out_19));

  // Notes on the sheet:
  //   Felipe Gabriel de Carvalho - 1543536
endmodule

// HA
module Half_Difference (
  input  in_1,
  input  in_2,
  output Diff,
  output Carr
);

  wire not_1_out;

  not not_1 (not_1_out, in_1);
  xor xor_1 (Diff, in_1, in_2);
  and and_1 (Carr, in_2, not_1_out);
endmodule

// FD
module Full_Difference (
  input  in_1,
  input  in_2,
  input  in_3,
  output Diff,
  output CarryOut
);

  wire half_difference_1_carr, half_difference_1_diff, half_difference_2_carr;

  Half_Difference half_difference_1 (
    .in_1(in_2), .in_2(in_3), .Diff(half_difference_1_diff), .Carr(half_difference_1_carr));
  Half_Difference half_difference_2 (
    .in_1(in_1), .in_2(half_difference_1_diff), .Diff(Diff), .Carr(half_difference_2_carr));
  or or_1 (CarryOut, half_difference_2_carr, half_difference_1_carr);
endmodule
