// Logisim project Guia_0804.circ as structural Verilog: 2 circuits, main circuit main
module main (
  input  in_1,
  input  in_2,
  input  in_3,
  input  in_4,
  input  in_5,
  input  in_6,
  input  in_7,
  input  in_8,
  input  in_9,
  input  in_10,
  input  in_11,
  input  in_12,
  output out_13,
  output out_14,
  output out_15,
  output out_16,
  output out_17,
  output out_18
);

  Inequality_Comparator inequality_comparator_1 (.in_1(in_1), .in_2(in_2), .out_3(out_13));
  Inequality_Comparator inequality_comparator_2 (.in_1(in_3), .in_2(in_4), .out_3(out_14));
  Inequality_Comparator inequality_comparator_3 (.in_1(in_5), .in_2(in_6), .out_3(out_15));
  Inequality_Comparator inequality_comparator_4 (.in_1(in_7), .in_2(in_8), .out_3(out_16));
  Inequality_Comparator inequality_comparator_5 (.in_1(in_9), .in_2(in_10), .out_3(out_17));
  Inequality_Comparator inequality_comparator_6 (.in_1(in_11), .in_2(in_12), .out_3(out_18));

  // Notes on the sheet:
  //   Felipe Gabriel de Carvalho - 1543536
endmodule

// IC
module Inequality_Comparator (
  input  in_1,
  input  in_2,
  output out_3
);

  xor xor_1 (out_3, in_1, in_2);
endmodule
