// Logisim project Guia_0805.circ as structural Verilog: 4 circuits, main circuit main
module main (
  input  in_1,
  input  in_2,
  input  in_3,
  input  in_4,
  input  in_5,
  output out_6,
  output out_7,
  output out_8,
  output out_9,
  output out_10,
  output out_11
);

  wire complemento_de_1_1_out_6, complemento_de_1_1_out_7, complemento_de_1_1_out_8,
       complemento_de_1_1_out_9, complemento_de_1_1_out_10, full_adder_1_carryout, full_adder_2_carryout,
       full_adder_3_carryout, full_adder_4_carryout;

  Complemento_de_1 complemento_de_1_1 (
    .in_1(in_1), .in_2(in_2), .in_3(in_3), .in_4(in_4), .in_5(in_5), .out_6(complemento_de_1_1_out_6),
    .out_7(complemento_de_1_1_out_7), .out_8(complemento_de_1_1_out_8), .out_9(complemento_de_1_1_out_9),
    .out_10(complemento_de_1_1_out_10));
  Full_Adder full_adder_1 (
    .in_1(1'b0), .in_2(complemento_de_1_1_out_6), .in_3(1'b1), .Sum(out_6), .CarryOut(full_adder_1_carryout));
  Full_Adder full_adder_2 (
    .in_1(full_adder_1_carryout), .in_2(complemento_de_1_1_out_7), .in_3(1'b0), .Sum(out_7),
    .CarryOut(full_adder_2_carryout));
  Full_Adder full_adder_3 (
    .in_1(full_adder_2_carryout), .in_2(complemento_de_1_1_out_8), .in_3(1'b0), .Sum(out_8),
    .CarryOut(full_adder_3_carryout));
  Full_Adder full_adder_4 (
    .in_1(full_adder_3_carryout), .in_2(complemento_de_1_1_out_9), .in_3(1'b0), .Sum(out_9),
    .CarryOut(full_adder_4_carryout));
  Full_Adder full_adder_5 (
    .in_1(full_adder_4_carryout), .in_2(complemento_de_1_1_out_10), .in_3(1'b0), .Sum(out_10),
    .CarryOut(out_11));

  // Notes on the sheet:
  //   Felipe Gabriel de Carvalho - 1543536
endmodule

// HA
module Half_Adder (
  input  in_1,
  input  in_2,
  output sum,
  output carry
);

  xor xor_1 (sum, in_1, in_2);
  and and_1 (carry, in_1, in_2);
endmodule

// FA
module Full_Adder (
  input  in_1,
  input  in_2,
  input  in_3,
  output Sum,
  output CarryOut
);

  wire half_adder_1_carry, half_adder_1_sum, half_adder_2_carry;

  Half_Adder half_adder_1 (.in_1(in_2), .in_2(in_3), .sum(half_adder_1_sum), .carry(half_adder_1_carry));
  Half_Adder half_adder_2 (.in_1(in_1), .in_2(half_adder_1_sum), .sum(Sum), .carry(half_adder_2_carry));
  or or_1 (CarryOut, half_adder_2_carry, half_adder_1_carry);
endmodule

// C1
module Complemento_de_1 (
  input  in_1,
  input  in_2,
  input  in_3,
  input  in_4,
  input  in_5,
  output out_6,
  output out_7,
  output out_8,
  output out_9,
  output out_10
);

  not not_1 (out_6, in_1);
  not not_2 (out_7, in_2);
  not not_3 (out_8, in_3);
  not not_4 (out_9, in_4);
  not not_5 (out_10, in_5);
endmodule
