// Logisim project Guia_1100.circ as structural Verilog: 1 circuit, main circuit main
module main (
  input  in_1,
  input  in_2,
  output out_3,
  output out_4
);

  wire clock_1_out, d_ff_1_q, d_ff_2_q, d_ff_2_qn, d_ff_3_q, d_ff_4_q, d_ff_5_q, d_ff_6_q, d_ff_7_q,
       d_ff_7_qn, d_ff_8_q;

  Clock clock_1 (.out(clock_1_out));
  D_Flip_Flop d_ff_1 (.clk(clock_1_out), .D(in_1), .Q(d_ff_1_q), .reset(in_2));  // open: Qn, preset
  D_Flip_Flop d_ff_2 (.clk(clock_1_out), .D(d_ff_1_q), .Q(d_ff_2_q), .Qn(d_ff_2_qn), .reset(in_2));  // open: preset
  D_Flip_Flop d_ff_3 (.clk(clock_1_out), .D(in_1), .Q(d_ff_3_q), .reset(in_2));  // open: Qn, preset
  D_Flip_Flop d_ff_4 (.clk(clock_1_out), .D(d_ff_2_q), .Q(d_ff_4_q), .reset(in_2));  // open: Qn, preset
  and and_1 (out_3, d_ff_1_q, d_ff_2_qn, d_ff_4_q, d_ff_6_q);
  D_Flip_Flop d_ff_5 (.clk(clock_1_out), .D(d_ff_3_q), .Q(d_ff_5_q), .reset(in_2));  // open: Qn, preset
  D_Flip_Flop d_ff_6 (.clk(clock_1_out), .D(d_ff_4_q), .Q(d_ff_6_q), .reset(in_2));  // open: Qn, preset
  D_Flip_Flop d_ff_7 (.clk(clock_1_out), .D(d_ff_5_q), .Q(d_ff_7_q), .Qn(d_ff_7_qn), .reset(in_2));  // open: preset
  D_Flip_Flop d_ff_8 (.clk(clock_1_out), .D(d_ff_7_q), .Q(d_ff_8_q), .reset(in_2));  // open: Qn, preset
  and and_2 (out_4, d_ff_5_q, d_ff_7_qn, d_ff_7_q, d_ff_8_q);

  // Notes on the sheet:
  //   Felipe Gabriel de Carvalho - 1543536
endmodule
