// Logisim project Guia_1101.circ as structural Verilog: 1 circuit, main circuit main
module main (
  input  in_1,
  input  in_2,
  output out_3
);

  wire clock_1_out, d_ff_1_q, d_ff_1_qn, d_ff_2_q, d_ff_3_q, d_ff_3_qn, d_ff_4_q, d_ff_5_qn;

  Clock clock_1 (.out(clock_1_out));
  D_Flip_Flop #(.enable("true")) d_ff_1 (
    .clk(clock_1_out), .D(in_1), .Q(d_ff_1_q), .Qn(d_ff_1_qn), .en(d_ff_5_qn), .reset(in_2));  // open: preset
  D_Flip_Flop #(.enable("true")) d_ff_2 (
    .clk(clock_1_out), .D(d_ff_1_q), .Q(d_ff_2_q), .en(d_ff_5_qn), .reset(in_2));  // open: Qn, preset
  D_Flip_Flop #(.enable("true")) d_ff_3 (
    .clk(clock_1_out), .D(d_ff_2_q), .Q(d_ff_3_q), .Qn(d_ff_3_qn), .en(d_ff_5_qn), .reset(in_2));  // open: preset
  D_Flip_Flop #(.enable("true")) d_ff_4 (
    .clk(clock_1_out), .D(d_ff_3_q), .Q(d_ff_4_q), .en(d_ff_5_qn), .reset(in_2));  // open: Qn, preset
  and and_1 (out_3, d_ff_4_q, d_ff_3_qn, d_ff_2_q, d_ff_1_qn);
  D_Flip_Flop #(.trigger("falling"), .enable("true")) d_ff_5 (
    .clk(clock_1_out), .D(out_3), .Qn(d_ff_5_qn), .en(d_ff_5_qn), .reset(in_2));  // open: Q, preset

  // Notes on the sheet:
  //   Felipe Gabriel de Carvalho - 1543536
endmodule
