// Logisim project Guia_1103.circ as structural Verilog: 1 circuit, main circuit main
module main (
  input  in_1,
  input  in_2,
  output [1:0] out_3
);

  wire and_1_out, clock_1_out, counter_1_carry, d_ff_1_q, d_ff_1_qn, d_ff_2_q, d_ff_3_q, d_ff_3_qn, d_ff_4_q,
       not_1_out;

  Clock clock_1 (.out(clock_1_out));
  D_Flip_Flop #(.enable("true")) d_ff_1 (
    .clk(clock_1_out), .D(in_1), .Q(d_ff_1_q), .Qn(d_ff_1_qn), .en(not_1_out), .reset(in_2));  // open: preset
  D_Flip_Flop #(.enable("true")) d_ff_2 (
    .clk(clock_1_out), .D(d_ff_1_q), .Q(d_ff_2_q), .en(not_1_out), .reset(in_2));  // open: Qn, preset
  D_Flip_Flop #(.enable("true")) d_ff_3 (
    .clk(clock_1_out), .D(d_ff_2_q), .Q(d_ff_3_q), .Qn(d_ff_3_qn), .en(not_1_out), .reset(in_2));  // open: preset
  D_Flip_Flop #(.enable("true")) d_ff_4 (
    .clk(clock_1_out), .D(d_ff_3_q), .Q(d_ff_4_q), .en(not_1_out), .reset(in_2));  // open: Qn, preset
  Counter #(.width(2), .max('h3)) counter_1 (
    .count(not_1_out), .Q(out_3), .carry(counter_1_carry), .clk(and_1_out), .clr(in_2));  // open: load, D, preset, down
  not not_1 (not_1_out, counter_1_carry);
  and and_1 (and_1_out, d_ff_4_q, d_ff_3_qn, d_ff_2_q, d_ff_1_qn);

  // Notes on the sheet:
  //   Felipe Gabriel de Carvalho - 1543536
endmodule
