// Logisim project Guia_1202.circ as structural Verilog: 1 circuit, main circuit main
module main (
  input  CLR,
  input  R_W,
  input  ADDR,
  output out_4
);

  wire and_1_out, and_2_out, CLK_out, j_k_ff_1_q, j_k_ff_1_qn, j_k_ff_2_q, j_k_ff_2_qn, j_k_ff_3_q,
       j_k_ff_3_qn, j_k_ff_4_q, j_k_ff_4_qn, j_k_ff_5_q, j_k_ff_5_qn, j_k_ff_6_q, j_k_ff_6_qn, j_k_ff_7_q,
       j_k_ff_7_qn, not_1_out;

  Clock CLK (.out(CLK_out));
  and and_1 (and_1_out, R_W, ADDR);
  not not_1 (not_1_out, ADDR);
  and and_2 (and_2_out, R_W, not_1_out);
  J_K_Flip_Flop j_k_ff_1 (
    .J(and_1_out), .clk(CLK_out), .K(and_2_out), .Q(j_k_ff_1_q), .Qn(j_k_ff_1_qn), .reset(CLR));  // open: preset
  J_K_Flip_Flop j_k_ff_2 (
    .J(j_k_ff_1_q), .clk(CLK_out), .K(j_k_ff_1_qn), .Q(j_k_ff_2_q), .Qn(j_k_ff_2_qn), .reset(CLR));  // open: preset
  J_K_Flip_Flop j_k_ff_3 (
    .J(j_k_ff_2_q), .clk(CLK_out), .K(j_k_ff_2_qn), .Q(j_k_ff_3_q), .Qn(j_k_ff_3_qn), .reset(CLR));  // open: preset
  J_K_Flip_Flop j_k_ff_4 (
    .J(j_k_ff_3_q), .clk(CLK_out), .K(j_k_ff_3_qn), .Q(j_k_ff_4_q), .Qn(j_k_ff_4_qn), .reset(CLR));  // open: preset
  J_K_Flip_Flop j_k_ff_5 (
    .J(j_k_ff_4_q), .clk(CLK_out), .K(j_k_ff_4_qn), .Q(j_k_ff_5_q), .Qn(j_k_ff_5_qn), .reset(CLR));  // open: preset
  J_K_Flip_Flop j_k_ff_6 (
    .J(j_k_ff_5_q), .clk(CLK_out), .K(j_k_ff_5_qn), .Q(j_k_ff_6_q), .Qn(j_k_ff_6_qn), .reset(CLR));  // open: preset
  J_K_Flip_Flop j_k_ff_7 (
    .J(j_k_ff_6_q), .clk(CLK_out), .K(j_k_ff_6_qn), .Q(j_k_ff_7_q), .Qn(j_k_ff_7_qn), .reset(CLR));  // open: preset
  J_K_Flip_Flop j_k_ff_8 (.J(j_k_ff_7_q), .clk(CLK_out), .K(j_k_ff_7_qn), .Q(out_4), .reset(CLR));  // open: Qn, preset

  // Notes on the sheet:
  //   Felipe Gabriel de Carvalho - 1543536
endmodule
