// Logisim project Guia_1203.circ as structural Verilog: 1 circuit, main circuit main
module main (
  input  ADDR,
  input  ADDR_2,
  input  CLR,
  input  R_W,
  output out_5,
  output out_6
);

  wire and_1_out, and_2_out, and_3_out, and_4_out, CLK_out, j_k_ff_1_q, j_k_ff_1_qn, j_k_ff_2_q, j_k_ff_2_qn,
       j_k_ff_3_q, j_k_ff_3_qn, j_k_ff_4_q, j_k_ff_4_qn, j_k_ff_5_q, j_k_ff_5_qn, j_k_ff_6_q, j_k_ff_6_qn,
       j_k_ff_7_q, j_k_ff_7_qn, j_k_ff_8_q, j_k_ff_8_qn, j_k_ff_9_q, j_k_ff_9_qn, j_k_ff_10_q, j_k_ff_10_qn,
       j_k_ff_11_q, j_k_ff_11_qn, j_k_ff_12_q, j_k_ff_12_qn, j_k_ff_13_q, j_k_ff_13_qn, j_k_ff_14_q,
       j_k_ff_14_qn, not_1_out, not_2_out;

  not not_1 (not_1_out, ADDR_2);
  and and_1 (and_1_out, R_W, not_1_out);
  Clock CLK (.out(CLK_out));
  and and_2 (and_2_out, ADDR_2, R_W);
  and and_3 (and_3_out, R_W, ADDR);
  not not_2 (not_2_out, ADDR);
  and and_4 (and_4_out, R_W, not_2_out);
  J_K_Flip_Flop j_k_ff_1 (
    .J(and_2_out), .clk(CLK_out), .K(and_1_out), .Q(j_k_ff_1_q), .Qn(j_k_ff_1_qn), .reset(CLR));  // open: preset
  J_K_Flip_Flop j_k_ff_2 (
    .J(and_3_out), .clk(CLK_out), .K(and_4_out), .Q(j_k_ff_2_q), .Qn(j_k_ff_2_qn), .reset(CLR));  // open: preset
  J_K_Flip_Flop j_k_ff_3 (
    .J(j_k_ff_1_q), .clk(CLK_out), .K(j_k_ff_1_qn), .Q(j_k_ff_3_q), .Qn(j_k_ff_3_qn), .reset(CLR));  // open: preset
  J_K_Flip_Flop j_k_ff_4 (
    .J(j_k_ff_2_q), .clk(CLK_out), .K(j_k_ff_2_qn), .Q(j_k_ff_4_q), .Qn(j_k_ff_4_qn), .reset(CLR));  // open: preset
  J_K_Flip_Flop j_k_ff_5 (
    .J(j_k_ff_3_q), .clk(CLK_out), .K(j_k_ff_3_qn), .Q(j_k_ff_5_q), .Qn(j_k_ff_5_qn), .reset(CLR));  // open: preset
  J_K_Flip_Flop j_k_ff_6 (
    .J(j_k_ff_4_q), .clk(CLK_out), .K(j_k_ff_4_qn), .Q(j_k_ff_6_q), .Qn(j_k_ff_6_qn), .reset(CLR));  // open: preset
  J_K_Flip_Flop j_k_ff_7 (
    .J(j_k_ff_5_q), .clk(CLK_out), .K(j_k_ff_5_qn), .Q(j_k_ff_7_q), .Qn(j_k_ff_7_qn), .reset(CLR));  // open: preset
  J_K_Flip_Flop j_k_ff_8 (
    .J(j_k_ff_6_q), .clk(CLK_out), .K(j_k_ff_6_qn), .Q(j_k_ff_8_q), .Qn(j_k_ff_8_qn), .reset(CLR));  // open: preset
  J_K_Flip_Flop j_k_ff_9 (
    .J(j_k_ff_7_q), .clk(CLK_out), .K(j_k_ff_7_qn), .Q(j_k_ff_9_q), .Qn(j_k_ff_9_qn), .reset(CLR));  // open: preset
  J_K_Flip_Flop j_k_ff_10 (
    .J(j_k_ff_8_q), .clk(CLK_out), .K(j_k_ff_8_qn), .Q(j_k_ff_10_q), .Qn(j_k_ff_10_qn), .reset(CLR));  // open: preset
  J_K_Flip_Flop j_k_ff_11 (
    .J(j_k_ff_9_q), .clk(CLK_out), .K(j_k_ff_9_qn), .Q(j_k_ff_11_q), .Qn(j_k_ff_11_qn), .reset(CLR));  // open: preset
  J_K_Flip_Flop j_k_ff_12 (
    .J(j_k_ff_10_q), .clk(CLK_out), .K(j_k_ff_10_qn), .Q(j_k_ff_12_q), .Qn(j_k_ff_12_qn), .reset(CLR));  // open: preset
  J_K_Flip_Flop j_k_ff_13 (
    .J(j_k_ff_12_q), .clk(CLK_out), .K(j_k_ff_12_qn), .Q(j_k_ff_13_q), .Qn(j_k_ff_13_qn), .reset(CLR));  // open: preset
  J_K_Flip_Flop j_k_ff_14 (
    .J(j_k_ff_11_q), .clk(CLK_out), .K(j_k_ff_11_qn), .Q(j_k_ff_14_q), .Qn(j_k_ff_14_qn), .reset(CLR));  // open: preset
  J_K_Flip_Flop j_k_ff_15 (
    .J(j_k_ff_14_q), .clk(CLK_out), .K(j_k_ff_14_qn), .Q(out_5), .reset(CLR));  // open: Qn, preset
  J_K_Flip_Flop j_k_ff_16 (
    .J(j_k_ff_13_q), .clk(CLK_out), .K(j_k_ff_13_qn), .Q(out_6), .reset(CLR));  // open: Qn, preset

  // Notes on the sheet:
  //   Felipe Gabriel de Carvalho - 1543536
endmodule
