// Logisim project Guia_1204.circ as structural Verilog: 1 circuit, main circuit main
module main (
  input  R_W,
  input  CLR,
  input  ADDR,
  input  ADDR_2,
  input  ADDR_3,
  input  ADDR_4,
  output out_7,
  output out_8,
  output out_9,
  output out_10
);

  wire and_1_out, and_2_out, and_3_out, and_4_out, and_5_out, and_6_out, and_7_out, and_8_out, CLK_out,
       j_k_ff_1_q, j_k_ff_1_qn, j_k_ff_2_q, j_k_ff_2_qn, j_k_ff_3_q, j_k_ff_3_qn, j_k_ff_4_q, j_k_ff_4_qn,
       j_k_ff_5_q, j_k_ff_5_qn, j_k_ff_6_q, j_k_ff_6_qn, j_k_ff_7_q, j_k_ff_7_qn, j_k_ff_8_q, j_k_ff_8_qn,
       j_k_ff_9_q, j_k_ff_9_qn, j_k_ff_10_q, j_k_ff_10_qn, j_k_ff_11_q, j_k_ff_11_qn, j_k_ff_12_q,
       j_k_ff_12_qn, j_k_ff_13_q, j_k_ff_13_qn, j_k_ff_14_q, j_k_ff_14_qn, j_k_ff_15_q, j_k_ff_15_qn,
       j_k_ff_16_q, j_k_ff_16_qn, j_k_ff_17_q, j_k_ff_17_qn, j_k_ff_18_q, j_k_ff_18_qn, j_k_ff_19_q,
       j_k_ff_19_qn, j_k_ff_20_q, j_k_ff_20_qn, j_k_ff_21_q, j_k_ff_21_qn, j_k_ff_22_q, j_k_ff_22_qn,
       j_k_ff_23_q, j_k_ff_23_qn, j_k_ff_24_q, j_k_ff_24_qn, j_k_ff_25_q, j_k_ff_25_qn, j_k_ff_26_q,
       j_k_ff_26_qn, j_k_ff_27_q, j_k_ff_27_qn, j_k_ff_28_q, j_k_ff_28_qn, not_1_out, not_2_out, not_3_out,
       not_4_out;

  Clock CLK (.out(CLK_out));
  not not_1 (not_1_out, ADDR_4);
  not not_2 (not_2_out, ADDR_2);
  and and_1 (and_1_out, R_W, not_1_out);
  and and_2 (and_2_out, R_W, not_2_out);
  and and_3 (and_3_out, ADDR_4, R_W);
  and and_4 (and_4_out, R_W, ADDR_3);
  and and_5 (and_5_out, R_W, not_3_out);
  not not_3 (not_3_out, ADDR_3);
  and and_6 (and_6_out, ADDR_2, R_W);
  and and_7 (and_7_out, R_W, ADDR);
  and and_8 (and_8_out, R_W, not_4_out);
  not not_4 (not_4_out, ADDR);
  J_K_Flip_Flop j_k_ff_1 (
    .J(and_3_out), .clk(CLK_out), .K(and_1_out), .Q(j_k_ff_1_q), .Qn(j_k_ff_1_qn), .reset(CLR));  // open: preset
  J_K_Flip_Flop j_k_ff_2 (
    .J(and_4_out), .clk(CLK_out), .K(and_5_out), .Q(j_k_ff_2_q), .Qn(j_k_ff_2_qn), .reset(CLR));  // open: preset
  J_K_Flip_Flop j_k_ff_3 (
    .J(and_6_out), .clk(CLK_out), .K(and_2_out), .Q(j_k_ff_3_q), .Qn(j_k_ff_3_qn), .reset(CLR));  // open: preset
  J_K_Flip_Flop j_k_ff_4 (
    .J(and_7_out), .clk(CLK_out), .K(and_8_out), .Q(j_k_ff_4_q), .Qn(j_k_ff_4_qn), .reset(CLR));  // open: preset
  J_K_Flip_Flop j_k_ff_5 (
    .J(j_k_ff_1_q), .clk(CLK_out), .K(j_k_ff_1_qn), .Q(j_k_ff_5_q), .Qn(j_k_ff_5_qn), .reset(CLR));  // open: preset
  J_K_Flip_Flop j_k_ff_6 (
    .J(j_k_ff_2_q), .clk(CLK_out), .K(j_k_ff_2_qn), .Q(j_k_ff_6_q), .Qn(j_k_ff_6_qn), .reset(CLR));  // open: preset
  J_K_Flip_Flop j_k_ff_7 (
    .J(j_k_ff_3_q), .clk(CLK_out), .K(j_k_ff_3_qn), .Q(j_k_ff_7_q), .Qn(j_k_ff_7_qn), .reset(CLR));  // open: preset
  J_K_Flip_Flop j_k_ff_8 (
    .J(j_k_ff_4_q), .clk(CLK_out), .K(j_k_ff_4_qn), .Q(j_k_ff_8_q), .Qn(j_k_ff_8_qn), .reset(CLR));  // open: preset
  J_K_Flip_Flop j_k_ff_9 (
    .J(j_k_ff_5_q), .clk(CLK_out), .K(j_k_ff_5_qn), .Q(j_k_ff_9_q), .Qn(j_k_ff_9_qn), .reset(CLR));  // open: preset
  J_K_Flip_Flop j_k_ff_10 (
    .J(j_k_ff_6_q), .clk(CLK_out), .K(j_k_ff_6_qn), .Q(j_k_ff_10_q), .Qn(j_k_ff_10_qn), .reset(CLR));  // open: preset
  J_K_Flip_Flop j_k_ff_11 (
    .J(j_k_ff_7_q), .clk(CLK_out), .K(j_k_ff_7_qn), .Q(j_k_ff_11_q), .Qn(j_k_ff_11_qn), .reset(CLR));  // open: preset
  J_K_Flip_Flop j_k_ff_12 (
    .J(j_k_ff_8_q), .clk(CLK_out), .K(j_k_ff_8_qn), .Q(j_k_ff_12_q), .Qn(j_k_ff_12_qn), .reset(CLR));  // open: preset
  J_K_Flip_Flop j_k_ff_13 (
    .J(j_k_ff_10_q), .clk(CLK_out), .K(j_k_ff_10_qn), .Q(j_k_ff_13_q), .Qn(j_k_ff_13_qn), .reset(CLR));  // open: preset
  J_K_Flip_Flop j_k_ff_14 (
    .J(j_k_ff_12_q), .clk(CLK_out), .K(j_k_ff_12_qn), .Q(j_k_ff_14_q), .Qn(j_k_ff_14_qn), .reset(CLR));  // open: preset
  J_K_Flip_Flop j_k_ff_15 (
    .J(j_k_ff_9_q), .clk(CLK_out), .K(j_k_ff_9_qn), .Q(j_k_ff_15_q), .Qn(j_k_ff_15_qn), .reset(CLR));  // open: preset
  J_K_Flip_Flop j_k_ff_16 (
    .J(j_k_ff_11_q), .clk(CLK_out), .K(j_k_ff_11_qn), .Q(j_k_ff_16_q), .Qn(j_k_ff_16_qn), .reset(CLR));  // open: preset
  J_K_Flip_Flop j_k_ff_17 (
    .J(j_k_ff_15_q), .clk(CLK_out), .K(j_k_ff_15_qn), .Q(j_k_ff_17_q), .Qn(j_k_ff_17_qn), .reset(CLR));  // open: preset
  J_K_Flip_Flop j_k_ff_18 (
    .J(j_k_ff_13_q), .clk(CLK_out), .K(j_k_ff_13_qn), .Q(j_k_ff_18_q), .Qn(j_k_ff_18_qn), .reset(CLR));  // open: preset
  J_K_Flip_Flop j_k_ff_19 (
    .J(j_k_ff_16_q), .clk(CLK_out), .K(j_k_ff_16_qn), .Q(j_k_ff_19_q), .Qn(j_k_ff_19_qn), .reset(CLR));  // open: preset
  J_K_Flip_Flop j_k_ff_20 (
    .J(j_k_ff_14_q), .clk(CLK_out), .K(j_k_ff_14_qn), .Q(j_k_ff_20_q), .Qn(j_k_ff_20_qn), .reset(CLR));  // open: preset
  J_K_Flip_Flop j_k_ff_21 (
    .J(j_k_ff_17_q), .clk(CLK_out), .K(j_k_ff_17_qn), .Q(j_k_ff_21_q), .Qn(j_k_ff_21_qn), .reset(CLR));  // open: preset
  J_K_Flip_Flop j_k_ff_22 (
    .J(j_k_ff_18_q), .clk(CLK_out), .K(j_k_ff_18_qn), .Q(j_k_ff_22_q), .Qn(j_k_ff_22_qn), .reset(CLR));  // open: preset
  J_K_Flip_Flop j_k_ff_23 (
    .J(j_k_ff_19_q), .clk(CLK_out), .K(j_k_ff_19_qn), .Q(j_k_ff_23_q), .Qn(j_k_ff_23_qn), .reset(CLR));  // open: preset
  J_K_Flip_Flop j_k_ff_24 (
    .J(j_k_ff_20_q), .clk(CLK_out), .K(j_k_ff_20_qn), .Q(j_k_ff_24_q), .Qn(j_k_ff_24_qn), .reset(CLR));  // open: preset
  J_K_Flip_Flop j_k_ff_25 (
    .J(j_k_ff_21_q), .clk(CLK_out), .K(j_k_ff_21_qn), .Q(j_k_ff_25_q), .Qn(j_k_ff_25_qn), .reset(CLR));  // open: preset
  J_K_Flip_Flop j_k_ff_26 (
    .J(j_k_ff_22_q), .clk(CLK_out), .K(j_k_ff_22_qn), .Q(j_k_ff_26_q), .Qn(j_k_ff_26_qn), .reset(CLR));  // open: preset
  J_K_Flip_Flop j_k_ff_27 (
    .J(j_k_ff_23_q), .clk(CLK_out), .K(j_k_ff_23_qn), .Q(j_k_ff_27_q), .Qn(j_k_ff_27_qn), .reset(CLR));  // open: preset
  J_K_Flip_Flop j_k_ff_28 (
    .J(j_k_ff_24_q), .clk(CLK_out), .K(j_k_ff_24_qn), .Q(j_k_ff_28_q), .Qn(j_k_ff_28_qn), .reset(CLR));  // open: preset
  J_K_Flip_Flop j_k_ff_29 (
    .J(j_k_ff_25_q), .clk(CLK_out), .K(j_k_ff_25_qn), .Q(out_7), .reset(CLR));  // open: Qn, preset
  J_K_Flip_Flop j_k_ff_30 (
    .J(j_k_ff_26_q), .clk(CLK_out), .K(j_k_ff_26_qn), .Q(out_8), .reset(CLR));  // open: Qn, preset
  J_K_Flip_Flop j_k_ff_31 (
    .J(j_k_ff_27_q), .clk(CLK_out), .K(j_k_ff_27_qn), .Q(out_9), .reset(CLR));  // open: Qn, preset
  J_K_Flip_Flop j_k_ff_32 (
    .J(j_k_ff_28_q), .clk(CLK_out), .K(j_k_ff_28_qn), .Q(out_10), .reset(CLR));  // open: Qn, preset

  // Notes on the sheet:
  //   Felipe Gabriel de Carvalho - 1543536
endmodule
