// Logisim project Guia_1205.circ as structural Verilog: 1 circuit, main circuit main
module main (
  input  ADDR,
  input  ADDR_2,
  input  ADDR_3,
  input  ADDR_4,
  input  R_W,
  input  CLR,
  input  ADDR_5,
  input  ADDR_6,
  input  ADDR_7,
  input  ADDR_8,
  output out_11,
  output out_12,
  output out_13,
  output out_14,
  output out_15,
  output out_16,
  output out_17,
  output out_18
);

  wire and_1_out, and_2_out, and_3_out, and_4_out, and_5_out, and_6_out, and_7_out, and_8_out, and_9_out,
       and_10_out, and_11_out, and_12_out, and_13_out, and_14_out, and_15_out, CLK_out, j_k_ff_1_q,
       j_k_ff_1_qn, j_k_ff_2_q, j_k_ff_2_qn, j_k_ff_3_q, j_k_ff_3_qn, j_k_ff_4_q, j_k_ff_4_qn, j_k_ff_5_q,
       j_k_ff_5_qn, j_k_ff_6_q, j_k_ff_6_qn, j_k_ff_7_q, j_k_ff_7_qn, j_k_ff_8_q, j_k_ff_8_qn, j_k_ff_9_q,
       j_k_ff_9_qn, j_k_ff_10_q, j_k_ff_10_qn, j_k_ff_11_q, j_k_ff_11_qn, j_k_ff_12_q, j_k_ff_12_qn,
       j_k_ff_13_q, j_k_ff_13_qn, j_k_ff_14_q, j_k_ff_14_qn, j_k_ff_15_q, j_k_ff_15_qn, j_k_ff_16_q,
       j_k_ff_16_qn, j_k_ff_17_q, j_k_ff_17_qn, j_k_ff_18_q, j_k_ff_18_qn, j_k_ff_19_q, j_k_ff_19_qn,
       j_k_ff_20_q, j_k_ff_20_qn, j_k_ff_21_q, j_k_ff_21_qn, j_k_ff_22_q, j_k_ff_22_qn, j_k_ff_23_q,
       j_k_ff_23_qn, j_k_ff_24_q, j_k_ff_24_qn, j_k_ff_25_q, j_k_ff_25_qn, j_k_ff_26_q, j_k_ff_26_qn,
       j_k_ff_27_q, j_k_ff_27_qn, j_k_ff_28_q, j_k_ff_28_qn, j_k_ff_29_q, j_k_ff_29_qn, j_k_ff_30_q,
       j_k_ff_30_qn, j_k_ff_31_q, j_k_ff_31_qn, j_k_ff_32_q, j_k_ff_32_qn, j_k_ff_33_q, j_k_ff_33_qn,
       j_k_ff_34_q, j_k_ff_34_qn, j_k_ff_35_q, j_k_ff_35_qn, j_k_ff_36_q, j_k_ff_36_qn, j_k_ff_37_q,
       j_k_ff_37_qn, j_k_ff_38_q, j_k_ff_38_qn, j_k_ff_39_q, j_k_ff_39_qn, j_k_ff_40_q, j_k_ff_40_qn,
       j_k_ff_41_q, j_k_ff_41_qn, j_k_ff_42_q, j_k_ff_42_qn, j_k_ff_43_q, j_k_ff_43_qn, j_k_ff_44_q,
       j_k_ff_44_qn, j_k_ff_45_q, j_k_ff_45_qn, j_k_ff_46_q, j_k_ff_46_qn, j_k_ff_47_q, j_k_ff_47_qn,
       j_k_ff_48_q, j_k_ff_48_qn, j_k_ff_49_q, j_k_ff_49_qn, j_k_ff_50_q, j_k_ff_50_qn, j_k_ff_51_q,
       j_k_ff_51_qn, j_k_ff_52_q, j_k_ff_52_qn, j_k_ff_53_q, j_k_ff_53_qn, j_k_ff_54_q, j_k_ff_54_qn,
       j_k_ff_55_q, j_k_ff_55_qn, j_k_ff_56_q, j_k_ff_56_qn, not_1_out, not_2_out, not_3_out, not_4_out,
       not_5_out, not_6_out, not_7_out;

  Clock CLK (.out(CLK_out));
  not not_1 (not_1_out, ADDR_8);
  not not_2 (not_2_out, ADDR_6);
  not not_3 (not_3_out, ADDR_4);
  not not_4 (not_4_out, ADDR_2);
  and and_1 (and_1_out, R_W, not_1_out);
  and and_2 (and_2_out, R_W, not_2_out);
  and and_3 (and_3_out, R_W, not_3_out);
  and and_4 (and_4_out, R_W, not_4_out);
  and and_5 (and_5_out, ADDR_8, R_W);
  and and_6 (and_6_out, R_W, ADDR_7);
  and and_7 (and_7_out, R_W, not_5_out);
  not not_5 (not_5_out, ADDR_7);
  and and_8 (and_8_out, ADDR_6, R_W);
  and and_9 (and_9_out, R_W, ADDR_5);
  and and_10 (and_10_out, R_W, not_6_out);
  not not_6 (not_6_out, ADDR_5);
  and and_11 (and_11_out, ADDR_4, R_W);
  and and_12 (and_12_out, R_W, ADDR_3);
  and and_13 (and_13_out, R_W, not_7_out);
  not not_7 (not_7_out, ADDR_3);
  and and_14 (and_14_out, ADDR_2, R_W);
  and and_15 (and_15_out, R_W, ADDR);
  J_K_Flip_Flop j_k_ff_1 (
    .J(and_11_out), .clk(CLK_out), .K(and_3_out), .Q(j_k_ff_1_q), .Qn(j_k_ff_1_qn), .reset(CLR));  // open: preset
  J_K_Flip_Flop j_k_ff_2 (
    .J(and_12_out), .clk(CLK_out), .K(and_13_out), .Q(j_k_ff_2_q), .Qn(j_k_ff_2_qn), .reset(CLR));  // open: preset
  J_K_Flip_Flop j_k_ff_3 (
    .J(and_14_out), .clk(CLK_out), .K(and_4_out), .Q(j_k_ff_3_q), .Qn(j_k_ff_3_qn), .reset(CLR));  // open: preset
  J_K_Flip_Flop j_k_ff_4 (
    .J(and_15_out), .clk(CLK_out), .K(R_W), .Q(j_k_ff_4_q), .Qn(j_k_ff_4_qn), .reset(CLR));  // open: preset
  J_K_Flip_Flop j_k_ff_5 (
    .J(and_5_out), .clk(CLK_out), .K(and_1_out), .Q(j_k_ff_5_q), .Qn(j_k_ff_5_qn), .reset(CLR));  // open: preset
  J_K_Flip_Flop j_k_ff_6 (
    .J(and_6_out), .clk(CLK_out), .K(and_7_out), .Q(j_k_ff_6_q), .Qn(j_k_ff_6_qn), .reset(CLR));  // open: preset
  J_K_Flip_Flop j_k_ff_7 (
    .J(and_8_out), .clk(CLK_out), .K(and_2_out), .Q(j_k_ff_7_q), .Qn(j_k_ff_7_qn), .reset(CLR));  // open: preset
  J_K_Flip_Flop j_k_ff_8 (
    .J(and_9_out), .clk(CLK_out), .K(and_10_out), .Q(j_k_ff_8_q), .Qn(j_k_ff_8_qn), .reset(CLR));  // open: preset
  J_K_Flip_Flop j_k_ff_9 (
    .J(j_k_ff_5_q), .clk(CLK_out), .K(j_k_ff_5_qn), .Q(j_k_ff_9_q), .Qn(j_k_ff_9_qn), .reset(CLR));  // open: preset
  J_K_Flip_Flop j_k_ff_10 (
    .J(j_k_ff_6_q), .clk(CLK_out), .K(j_k_ff_6_qn), .Q(j_k_ff_10_q), .Qn(j_k_ff_10_qn), .reset(CLR));  // open: preset
  J_K_Flip_Flop j_k_ff_11 (
    .J(j_k_ff_7_q), .clk(CLK_out), .K(j_k_ff_7_qn), .Q(j_k_ff_11_q), .Qn(j_k_ff_11_qn), .reset(CLR));  // open: preset
  J_K_Flip_Flop j_k_ff_12 (
    .J(j_k_ff_8_q), .clk(CLK_out), .K(j_k_ff_8_qn), .Q(j_k_ff_12_q), .Qn(j_k_ff_12_qn), .reset(CLR));  // open: preset
  J_K_Flip_Flop j_k_ff_13 (
    .J(j_k_ff_1_q), .clk(CLK_out), .K(j_k_ff_1_qn), .Q(j_k_ff_13_q), .Qn(j_k_ff_13_qn), .reset(CLR));  // open: preset
  J_K_Flip_Flop j_k_ff_14 (
    .J(j_k_ff_2_q), .clk(CLK_out), .K(j_k_ff_2_qn), .Q(j_k_ff_14_q), .Qn(j_k_ff_14_qn), .reset(CLR));  // open: preset
  J_K_Flip_Flop j_k_ff_15 (
    .J(j_k_ff_3_q), .clk(CLK_out), .K(j_k_ff_3_qn), .Q(j_k_ff_15_q), .Qn(j_k_ff_15_qn), .reset(CLR));  // open: preset
  J_K_Flip_Flop j_k_ff_16 (
    .J(j_k_ff_4_q), .clk(CLK_out), .K(j_k_ff_4_qn), .Q(j_k_ff_16_q), .Qn(j_k_ff_16_qn), .reset(CLR));  // open: preset
  J_K_Flip_Flop j_k_ff_17 (
    .J(j_k_ff_9_q), .clk(CLK_out), .K(j_k_ff_9_qn), .Q(j_k_ff_17_q), .Qn(j_k_ff_17_qn), .reset(CLR));  // open: preset
  J_K_Flip_Flop j_k_ff_18 (
    .J(j_k_ff_10_q), .clk(CLK_out), .K(j_k_ff_10_qn), .Q(j_k_ff_18_q), .Qn(j_k_ff_18_qn), .reset(CLR));  // open: preset
  J_K_Flip_Flop j_k_ff_19 (
    .J(j_k_ff_11_q), .clk(CLK_out), .K(j_k_ff_11_qn), .Q(j_k_ff_19_q), .Qn(j_k_ff_19_qn), .reset(CLR));  // open: preset
  J_K_Flip_Flop j_k_ff_20 (
    .J(j_k_ff_12_q), .clk(CLK_out), .K(j_k_ff_12_qn), .Q(j_k_ff_20_q), .Qn(j_k_ff_20_qn), .reset(CLR));  // open: preset
  J_K_Flip_Flop j_k_ff_21 (
    .J(j_k_ff_13_q), .clk(CLK_out), .K(j_k_ff_13_qn), .Q(j_k_ff_21_q), .Qn(j_k_ff_21_qn), .reset(CLR));  // open: preset
  J_K_Flip_Flop j_k_ff_22 (
    .J(j_k_ff_14_q), .clk(CLK_out), .K(j_k_ff_14_qn), .Q(j_k_ff_22_q), .Qn(j_k_ff_22_qn), .reset(CLR));  // open: preset
  J_K_Flip_Flop j_k_ff_23 (
    .J(j_k_ff_15_q), .clk(CLK_out), .K(j_k_ff_15_qn), .Q(j_k_ff_23_q), .Qn(j_k_ff_23_qn), .reset(CLR));  // open: preset
  J_K_Flip_Flop j_k_ff_24 (
    .J(j_k_ff_16_q), .clk(CLK_out), .K(j_k_ff_16_qn), .Q(j_k_ff_24_q), .Qn(j_k_ff_24_qn), .reset(CLR));  // open: preset
  J_K_Flip_Flop j_k_ff_25 (
    .J(j_k_ff_18_q), .clk(CLK_out), .K(j_k_ff_18_qn), .Q(j_k_ff_25_q), .Qn(j_k_ff_25_qn), .reset(CLR));  // open: preset
  J_K_Flip_Flop j_k_ff_26 (
    .J(j_k_ff_20_q), .clk(CLK_out), .K(j_k_ff_20_qn), .Q(j_k_ff_26_q), .Qn(j_k_ff_26_qn), .reset(CLR));  // open: preset
  J_K_Flip_Flop j_k_ff_27 (
    .J(j_k_ff_21_q), .clk(CLK_out), .K(j_k_ff_21_qn), .Q(j_k_ff_27_q), .Qn(j_k_ff_27_qn), .reset(CLR));  // open: preset
  J_K_Flip_Flop j_k_ff_28 (
    .J(j_k_ff_22_q), .clk(CLK_out), .K(j_k_ff_22_qn), .Q(j_k_ff_28_q), .Qn(j_k_ff_28_qn), .reset(CLR));  // open: preset
  J_K_Flip_Flop j_k_ff_29 (
    .J(j_k_ff_23_q), .clk(CLK_out), .K(j_k_ff_23_qn), .Q(j_k_ff_29_q), .Qn(j_k_ff_29_qn), .reset(CLR));  // open: preset
  J_K_Flip_Flop j_k_ff_30 (
    .J(j_k_ff_24_q), .clk(CLK_out), .K(j_k_ff_24_qn), .Q(j_k_ff_30_q), .Qn(j_k_ff_30_qn), .reset(CLR));  // open: preset
  J_K_Flip_Flop j_k_ff_31 (
    .J(j_k_ff_17_q), .clk(CLK_out), .K(j_k_ff_17_qn), .Q(j_k_ff_31_q), .Qn(j_k_ff_31_qn), .reset(CLR));  // open: preset
  J_K_Flip_Flop j_k_ff_32 (
    .J(j_k_ff_19_q), .clk(CLK_out), .K(j_k_ff_19_qn), .Q(j_k_ff_32_q), .Qn(j_k_ff_32_qn), .reset(CLR));  // open: preset
  J_K_Flip_Flop j_k_ff_33 (
    .J(j_k_ff_28_q), .clk(CLK_out), .K(j_k_ff_28_qn), .Q(j_k_ff_33_q), .Qn(j_k_ff_33_qn), .reset(CLR));  // open: preset
  J_K_Flip_Flop j_k_ff_34 (
    .J(j_k_ff_30_q), .clk(CLK_out), .K(j_k_ff_30_qn), .Q(j_k_ff_34_q), .Qn(j_k_ff_34_qn), .reset(CLR));  // open: preset
  J_K_Flip_Flop j_k_ff_35 (
    .J(j_k_ff_31_q), .clk(CLK_out), .K(j_k_ff_31_qn), .Q(j_k_ff_35_q), .Qn(j_k_ff_35_qn), .reset(CLR));  // open: preset
  J_K_Flip_Flop j_k_ff_36 (
    .J(j_k_ff_25_q), .clk(CLK_out), .K(j_k_ff_25_qn), .Q(j_k_ff_36_q), .Qn(j_k_ff_36_qn), .reset(CLR));  // open: preset
  J_K_Flip_Flop j_k_ff_37 (
    .J(j_k_ff_32_q), .clk(CLK_out), .K(j_k_ff_32_qn), .Q(j_k_ff_37_q), .Qn(j_k_ff_37_qn), .reset(CLR));  // open: preset
  J_K_Flip_Flop j_k_ff_38 (
    .J(j_k_ff_26_q), .clk(CLK_out), .K(j_k_ff_26_qn), .Q(j_k_ff_38_q), .Qn(j_k_ff_38_qn), .reset(CLR));  // open: preset
  J_K_Flip_Flop j_k_ff_39 (
    .J(j_k_ff_27_q), .clk(CLK_out), .K(j_k_ff_27_qn), .Q(j_k_ff_39_q), .Qn(j_k_ff_39_qn), .reset(CLR));  // open: preset
  J_K_Flip_Flop j_k_ff_40 (
    .J(j_k_ff_29_q), .clk(CLK_out), .K(j_k_ff_29_qn), .Q(j_k_ff_40_q), .Qn(j_k_ff_40_qn), .reset(CLR));  // open: preset
  J_K_Flip_Flop j_k_ff_41 (
    .J(j_k_ff_35_q), .clk(CLK_out), .K(j_k_ff_35_qn), .Q(j_k_ff_41_q), .Qn(j_k_ff_41_qn), .reset(CLR));  // open: preset
  J_K_Flip_Flop j_k_ff_42 (
    .J(j_k_ff_36_q), .clk(CLK_out), .K(j_k_ff_36_qn), .Q(j_k_ff_42_q), .Qn(j_k_ff_42_qn), .reset(CLR));  // open: preset
  J_K_Flip_Flop j_k_ff_43 (
    .J(j_k_ff_37_q), .clk(CLK_out), .K(j_k_ff_37_qn), .Q(j_k_ff_43_q), .Qn(j_k_ff_43_qn), .reset(CLR));  // open: preset
  J_K_Flip_Flop j_k_ff_44 (
    .J(j_k_ff_38_q), .clk(CLK_out), .K(j_k_ff_38_qn), .Q(j_k_ff_44_q), .Qn(j_k_ff_44_qn), .reset(CLR));  // open: preset
  J_K_Flip_Flop j_k_ff_45 (
    .J(j_k_ff_39_q), .clk(CLK_out), .K(j_k_ff_39_qn), .Q(j_k_ff_45_q), .Qn(j_k_ff_45_qn), .reset(CLR));  // open: preset
  J_K_Flip_Flop j_k_ff_46 (
    .J(j_k_ff_33_q), .clk(CLK_out), .K(j_k_ff_33_qn), .Q(j_k_ff_46_q), .Qn(j_k_ff_46_qn), .reset(CLR));  // open: preset
  J_K_Flip_Flop j_k_ff_47 (
    .J(j_k_ff_40_q), .clk(CLK_out), .K(j_k_ff_40_qn), .Q(j_k_ff_47_q), .Qn(j_k_ff_47_qn), .reset(CLR));  // open: preset
  J_K_Flip_Flop j_k_ff_48 (
    .J(j_k_ff_34_q), .clk(CLK_out), .K(j_k_ff_34_qn), .Q(j_k_ff_48_q), .Qn(j_k_ff_48_qn), .reset(CLR));  // open: preset
  J_K_Flip_Flop j_k_ff_49 (
    .J(j_k_ff_41_q), .clk(CLK_out), .K(j_k_ff_41_qn), .Q(j_k_ff_49_q), .Qn(j_k_ff_49_qn), .reset(CLR));  // open: preset
  J_K_Flip_Flop j_k_ff_50 (
    .J(j_k_ff_42_q), .clk(CLK_out), .K(j_k_ff_42_qn), .Q(j_k_ff_50_q), .Qn(j_k_ff_50_qn), .reset(CLR));  // open: preset
  J_K_Flip_Flop j_k_ff_51 (
    .J(j_k_ff_43_q), .clk(CLK_out), .K(j_k_ff_43_qn), .Q(j_k_ff_51_q), .Qn(j_k_ff_51_qn), .reset(CLR));  // open: preset
  J_K_Flip_Flop j_k_ff_52 (
    .J(j_k_ff_44_q), .clk(CLK_out), .K(j_k_ff_44_qn), .Q(j_k_ff_52_q), .Qn(j_k_ff_52_qn), .reset(CLR));  // open: preset
  J_K_Flip_Flop j_k_ff_53 (
    .J(j_k_ff_45_q), .clk(CLK_out), .K(j_k_ff_45_qn), .Q(j_k_ff_53_q), .Qn(j_k_ff_53_qn), .reset(CLR));  // open: preset
  J_K_Flip_Flop j_k_ff_54 (
    .J(j_k_ff_46_q), .clk(CLK_out), .K(j_k_ff_46_qn), .Q(j_k_ff_54_q), .Qn(j_k_ff_54_qn), .reset(CLR));  // open: preset
  J_K_Flip_Flop j_k_ff_55 (
    .J(j_k_ff_47_q), .clk(CLK_out), .K(j_k_ff_47_qn), .Q(j_k_ff_55_q), .Qn(j_k_ff_55_qn), .reset(CLR));  // open: preset
  J_K_Flip_Flop j_k_ff_56 (
    .J(j_k_ff_48_q), .clk(CLK_out), .K(j_k_ff_48_qn), .Q(j_k_ff_56_q), .Qn(j_k_ff_56_qn), .reset(CLR));  // open: preset
  J_K_Flip_Flop j_k_ff_57 (
    .J(j_k_ff_53_q), .clk(CLK_out), .K(j_k_ff_53_qn), .Q(out_15), .reset(CLR));  // open: Qn, preset
  J_K_Flip_Flop j_k_ff_58 (
    .J(j_k_ff_54_q), .clk(CLK_out), .K(j_k_ff_54_qn), .Q(out_16), .reset(CLR));  // open: Qn, preset
  J_K_Flip_Flop j_k_ff_59 (
    .J(j_k_ff_55_q), .clk(CLK_out), .K(j_k_ff_55_qn), .Q(out_17), .reset(CLR));  // open: Qn, preset
  J_K_Flip_Flop j_k_ff_60 (
    .J(j_k_ff_56_q), .clk(CLK_out), .K(j_k_ff_56_qn), .Q(out_18), .reset(CLR));  // open: Qn, preset
  J_K_Flip_Flop j_k_ff_61 (
    .J(j_k_ff_49_q), .clk(CLK_out), .K(j_k_ff_49_qn), .Q(out_11), .reset(CLR));  // open: Qn, preset
  J_K_Flip_Flop j_k_ff_62 (
    .J(j_k_ff_50_q), .clk(CLK_out), .K(j_k_ff_50_qn), .Q(out_12), .reset(CLR));  // open: Qn, preset
  J_K_Flip_Flop j_k_ff_63 (
    .J(j_k_ff_51_q), .clk(CLK_out), .K(j_k_ff_51_qn), .Q(out_13), .reset(CLR));  // open: Qn, preset
  J_K_Flip_Flop j_k_ff_64 (
    .J(j_k_ff_52_q), .clk(CLK_out), .K(j_k_ff_52_qn), .Q(out_14), .reset(CLR));  // open: Qn, preset

  // Notes on the sheet:
  //   Felipe Gabriel de Carvalho - 1543536
endmodule
