// Logisim project Guia_1302.circ as structural Verilog: 1 circuit, main circuit main
module main (
  input  PULSO,
  input  CLR
);

  wire CLK_out, j_k_ff_1_qn, j_k_ff_2_q, j_k_ff_2_qn, j_k_ff_3_q, j_k_ff_3_qn, j_k_ff_4_q, j_k_ff_4_qn,
       j_k_ff_5_q, j_k_ff_5_qn, j_k_ff_6_q, j_k_ff_6_qn;

  Clock CLK (.out(CLK_out));
  // Probe on j_k_ff_1_qn
  J_K_Flip_Flop j_k_ff_1 (.J(PULSO), .clk(j_k_ff_2_q), .K(PULSO), .Qn(j_k_ff_1_qn), .reset(CLR));  // open: Q, preset
  // Probe on j_k_ff_2_qn
  J_K_Flip_Flop j_k_ff_2 (
    .J(PULSO), .clk(j_k_ff_3_q), .K(PULSO), .Q(j_k_ff_2_q), .Qn(j_k_ff_2_qn), .reset(CLR));  // open: preset
  // Probe on j_k_ff_3_qn
  J_K_Flip_Flop j_k_ff_3 (
    .J(PULSO), .clk(j_k_ff_4_q), .K(PULSO), .Q(j_k_ff_3_q), .Qn(j_k_ff_3_qn), .reset(CLR));  // open: preset
  // Probe on j_k_ff_4_qn
  J_K_Flip_Flop j_k_ff_4 (
    .J(PULSO), .clk(j_k_ff_5_q), .K(PULSO), .Q(j_k_ff_4_q), .Qn(j_k_ff_4_qn), .reset(CLR));  // open: preset
  // Probe on j_k_ff_5_qn
  J_K_Flip_Flop j_k_ff_5 (
    .J(PULSO), .clk(j_k_ff_6_q), .K(PULSO), .Q(j_k_ff_5_q), .Qn(j_k_ff_5_qn), .reset(CLR));  // open: preset
  // Probe on j_k_ff_6_qn
  J_K_Flip_Flop j_k_ff_6 (
    .J(PULSO), .clk(CLK_out), .K(PULSO), .Q(j_k_ff_6_q), .Qn(j_k_ff_6_qn), .reset(CLR));  // open: preset

  // Notes on the sheet:
  //   FELIPE GABRIEL DE CARVALHO - 1543536
endmodule
