// Logisim project Guia_1303.circ as structural Verilog: 1 circuit, main circuit main
module main (
  input  _1,
  input  CLR
);

  wire CLK_out, j_k_ff_1_q, j_k_ff_1_qn, j_k_ff_2_q, j_k_ff_2_qn, j_k_ff_3_q, j_k_ff_3_qn, j_k_ff_4_q,
       j_k_ff_4_qn, j_k_ff_5_q, nand_1_out, nand_2_out, not_1_out, not_2_out;

  Clock CLK (.out(CLK_out));
  nand nand_1 (nand_1_out, CLR, nand_2_out);
  nand nand_2 (nand_2_out, not_1_out, j_k_ff_2_q, j_k_ff_5_q, not_2_out, j_k_ff_4_q);
  not not_1 (not_1_out, j_k_ff_1_q);
  not not_2 (not_2_out, j_k_ff_3_q);
  // Probe on j_k_ff_5_q
  J_K_Flip_Flop j_k_ff_1 (
    .J(_1), .clk(CLK_out), .K(_1), .Q(j_k_ff_1_q), .Qn(j_k_ff_1_qn), .reset(nand_1_out));  // open: preset
  // Probe on j_k_ff_4_q
  J_K_Flip_Flop j_k_ff_2 (
    .J(_1), .clk(j_k_ff_1_qn), .K(_1), .Q(j_k_ff_2_q), .Qn(j_k_ff_2_qn), .reset(nand_1_out));  // open: preset
  // Probe on j_k_ff_3_q
  J_K_Flip_Flop j_k_ff_3 (
    .J(_1), .clk(j_k_ff_2_qn), .K(_1), .Q(j_k_ff_3_q), .Qn(j_k_ff_3_qn), .reset(nand_1_out));  // open: preset
  // Probe on j_k_ff_2_q
  J_K_Flip_Flop j_k_ff_4 (
    .J(_1), .clk(j_k_ff_3_qn), .K(_1), .Q(j_k_ff_4_q), .Qn(j_k_ff_4_qn), .reset(nand_1_out));  // open: preset
  // Probe on j_k_ff_1_q
  J_K_Flip_Flop j_k_ff_5 (.J(_1), .clk(j_k_ff_4_qn), .K(_1), .Q(j_k_ff_5_q), .reset(nand_1_out));  // open: Qn, preset

  // Notes on the sheet:
  //   FELIPE GABRIEL DE CARVALHO - 1543536
endmodule
