// Logisim project Guia_1304.circ as structural Verilog: 1 circuit, main circuit main
module main (
  input  _1
);

  wire CLK_out, j_k_ff_1_q, j_k_ff_1_qn, j_k_ff_2_q, j_k_ff_2_qn, j_k_ff_3_q, j_k_ff_3_qn, j_k_ff_4_q,
       j_k_ff_4_qn, j_k_ff_5_q, j_k_ff_5_qn, nand_1_out, not_1_out, not_2_out, not_3_out, not_4_out, or_1_out;

  Clock CLK (.out(CLK_out));
  not not_1 (not_1_out, _1);
  or or_1 (or_1_out, not_1_out, not_2_out);
  not not_2 (not_2_out, nand_1_out);
  nand nand_1 (nand_1_out, not_3_out, j_k_ff_2_qn, j_k_ff_5_qn, not_4_out, j_k_ff_4_qn);
  not not_3 (not_3_out, j_k_ff_1_qn);
  not not_4 (not_4_out, j_k_ff_3_qn);
  // Probe on j_k_ff_5_q
  J_K_Flip_Flop j_k_ff_1 (
    .J(_1), .clk(CLK_out), .K(_1), .Q(j_k_ff_1_q), .Qn(j_k_ff_1_qn), .reset(or_1_out));  // open: preset
  // Probe on j_k_ff_4_q
  J_K_Flip_Flop j_k_ff_2 (
    .J(_1), .clk(j_k_ff_1_q), .K(_1), .Q(j_k_ff_2_q), .Qn(j_k_ff_2_qn), .reset(or_1_out));  // open: preset
  // Probe on j_k_ff_3_q
  J_K_Flip_Flop j_k_ff_3 (
    .J(_1), .clk(j_k_ff_2_q), .K(_1), .Q(j_k_ff_3_q), .Qn(j_k_ff_3_qn), .reset(or_1_out));  // open: preset
  // Probe on j_k_ff_2_q
  J_K_Flip_Flop j_k_ff_4 (
    .J(_1), .clk(j_k_ff_3_q), .K(_1), .Q(j_k_ff_4_q), .Qn(j_k_ff_4_qn), .reset(or_1_out));  // open: preset
  // Probe on j_k_ff_1_q
  J_K_Flip_Flop j_k_ff_5 (
    .J(_1), .clk(j_k_ff_4_q), .K(_1), .Q(j_k_ff_5_q), .Qn(j_k_ff_5_qn), .reset(or_1_out));  // open: preset

  // Notes on the sheet:
  //   FELIPE GABRIEL DE CARVALHO - 1543536
endmodule
