// Logisim project Guia_1305.circ as structural Verilog: 1 circuit, main circuit main
module main (
  input  CLR
);

  wire and_1_out, clock_1_out, not_1_out, not_2_out, not_3_out, or_1_out, t_ff_1_q, t_ff_2_q, t_ff_2_qn,
       t_ff_3_q, t_ff_3_qn, t_ff_4_q, t_ff_4_qn, t_ff_5_q, t_ff_5_qn, t_ff_6_q, t_ff_6_qn, t_ff_7_q,
       t_ff_7_qn;

  Clock clock_1 (.out(clock_1_out));
  or or_1 (or_1_out, CLR, and_1_out);
  and and_1 (and_1_out, t_ff_4_q, not_1_out, t_ff_1_q, not_2_out, t_ff_3_q, t_ff_6_q, not_3_out);
  // Probe on t_ff_1_q
  T_Flip_Flop t_ff_1 (.clk(t_ff_2_qn), .T(t_ff_2_qn), .Q(t_ff_1_q), .reset(or_1_out));  // open: Qn, preset
  not not_1 (not_1_out, t_ff_5_q);
  not not_2 (not_2_out, t_ff_2_q);
  not not_3 (not_3_out, t_ff_7_q);
  // Probe on t_ff_2_q
  T_Flip_Flop t_ff_2 (.clk(t_ff_3_qn), .T(t_ff_3_qn), .Q(t_ff_2_q), .Qn(t_ff_2_qn), .reset(or_1_out));  // open: preset
  // Probe on t_ff_3_q
  T_Flip_Flop t_ff_3 (.clk(t_ff_4_qn), .T(t_ff_4_qn), .Q(t_ff_3_q), .Qn(t_ff_3_qn), .reset(or_1_out));  // open: preset
  // Probe on t_ff_4_q
  T_Flip_Flop t_ff_4 (.clk(t_ff_5_qn), .T(t_ff_5_qn), .Q(t_ff_4_q), .Qn(t_ff_4_qn), .reset(or_1_out));  // open: preset
  T_Flip_Flop t_ff_5 (.clk(t_ff_6_qn), .T(t_ff_6_qn), .Q(t_ff_5_q), .Qn(t_ff_5_qn), .reset(or_1_out));  // open: preset
  // Probe on t_ff_5_q
  // Probe on t_ff_6_q
  T_Flip_Flop t_ff_6 (.clk(t_ff_7_qn), .T(t_ff_7_qn), .Q(t_ff_6_q), .Qn(t_ff_6_qn), .reset(or_1_out));  // open: preset
  // Probe on t_ff_7_q
  T_Flip_Flop t_ff_7 (
    .clk(clock_1_out), .T(clock_1_out), .Q(t_ff_7_q), .Qn(t_ff_7_qn), .reset(or_1_out));  // open: preset

  // Notes on the sheet:
  //   Felipe Gabriel de Carvalho - 1543536
endmodule
