// Logisim project Guia_1403.circ as structural Verilog: 1 circuit, main circuit main
module main (
  input  Input,
  input  Clear
);

  wire Clock_out, d_ff_1_q, d_ff_2_q, d_ff_3_q, d_ff_4_q, d_ff_5_q;

  Clock Clock (.out(Clock_out));
  // OR_Gate or_1 has open pins: in0=Input, out=open
  // Probe on d_ff_1_q
  D_Flip_Flop d_ff_1 (.clk(Clock_out), .D(d_ff_5_q), .Q(d_ff_1_q), .preset(Clear));  // open: Qn, reset
  // Probe on d_ff_2_q
  D_Flip_Flop d_ff_2 (.clk(Clock_out), .D(d_ff_1_q), .Q(d_ff_2_q), .reset(Clear));  // open: Qn, preset
  D_Flip_Flop d_ff_3 (.clk(Clock_out), .D(d_ff_2_q), .Q(d_ff_3_q), .reset(Clear));  // open: Qn, preset
  // Probe on d_ff_3_q
  // Probe on d_ff_4_q
  D_Flip_Flop d_ff_4 (.clk(Clock_out), .D(d_ff_3_q), .Q(d_ff_4_q), .reset(Clear));  // open: Qn, preset
  // Probe on d_ff_5_q
  D_Flip_Flop d_ff_5 (.clk(Clock_out), .D(d_ff_4_q), .Q(d_ff_5_q), .reset(Clear));  // open: Qn, preset

  // Notes on the sheet:
  //   Felipe Gabriel de Carvalho - 1543536
endmodule
