// Logisim project Guia_1405.circ as structural Verilog: 1 circuit, main circuit main
module main (
  input  in_1,
  input  in_2,
  input  in_3,
  input  in_4,
  input  in_5,
  input  Load,
  input  Clear
);

  wire and_1_out, and_2_out, and_3_out, and_4_out, and_5_out, Clock_out, d_ff_1_q, d_ff_2_q, d_ff_3_q,
       d_ff_4_q, d_ff_5_q;

  Clock Clock (.out(Clock_out));
  // Probe on d_ff_1_q
  and and_1 (and_1_out, Load, in_1);
  D_Flip_Flop d_ff_1 (.clk(Clock_out), .D(1'b0), .Q(d_ff_1_q), .preset(and_1_out), .reset(Clear));  // open: Qn
  and and_2 (and_2_out, Load, in_2);
  D_Flip_Flop d_ff_2 (.clk(Clock_out), .D(d_ff_1_q), .Q(d_ff_2_q), .preset(and_2_out), .reset(Clear));  // open: Qn
  // Probe on d_ff_2_q
  and and_3 (and_3_out, Load, in_3);
  // Probe on d_ff_3_q
  and and_4 (and_4_out, Load, in_4);
  D_Flip_Flop d_ff_3 (.clk(Clock_out), .D(d_ff_2_q), .Q(d_ff_3_q), .preset(and_3_out), .reset(Clear));  // open: Qn
  // Probe on d_ff_4_q
  D_Flip_Flop d_ff_4 (.clk(Clock_out), .D(d_ff_3_q), .Q(d_ff_4_q), .preset(and_4_out), .reset(Clear));  // open: Qn
  // Probe on d_ff_5_q
  and and_5 (and_5_out, Load, in_5);
  D_Flip_Flop d_ff_5 (.clk(Clock_out), .D(d_ff_4_q), .Q(d_ff_5_q), .preset(and_5_out), .reset(Clear));  // open: Qn

  // Notes on the sheet:
  //   Felipe Gabriel de Carvalho - 1543536
endmodule
